# Fritzing sketch UberPWM2 (saved by Fritzing 0.9.2b)
circuit board: 4.84164cm x 4.3091cm
breadboards: 1

parts:
  Q4 = TRANSISTOR_NPN [package=to-92-ammo]
  JP3 = Header 4 [package=molex-1x4_lock]
  Flyduino = Arduino Pro Mini v13
  Q5 = TRANSISTOR_NPN [package=to-92-ammo]
  JP5 = Header 4 [package=molex-1x4_lock]
  Q6 = TRANSISTOR_NPN [package=to-92-ammo]
  JP6 = Header 4 [package=molex-1x4_lock]
  Q7 = TRANSISTOR_NPN [package=to-92-ammo]
  JP7 = Header 4 [package=molex-1x4_lock]
  Q8 = TRANSISTOR_NPN [package=to-92-ammo]
  JP8 = Header 4 [package=molex-1x4_lock]
  Q9 = TRANSISTOR_NPN [package=to-92-ammo]
  JP10 = Header 4 [package=molex-1x4_lock]
  Q11 = TRANSISTOR_NPN [package=to-92-ammo]
  JP9 = Header 4 [package=molex-1x4_lock]
  R9 = Resistor [tolerance=±5% resistance=10k package=THT]
  R13 = Resistor [tolerance=±5% resistance=10k package=THT]
  R15 = Resistor [tolerance=±5% resistance=10k package=THT]
  R17 = Resistor [tolerance=±5% resistance=10k package=THT]
  R19 = Resistor [tolerance=±5% resistance=10k package=THT]
  R12 = Resistor [tolerance=±5% resistance=100k package=THT]
  R14 = Resistor [tolerance=±5% resistance=100k package=THT]
  R16 = Resistor [tolerance=±5% resistance=100k package=THT]
  R18 = Resistor [tolerance=±5% resistance=100k package=THT]
  R21 = Resistor [tolerance=±5% resistance=10k package=THT]
  J1 = COMPUTER-PERIPHERAL-POWER [package=computer-peripheral-power]
  Q10 = TRANSISTOR_NPN [package=to-92-ammo]
  R22 = Resistor [tolerance=±5% resistance=100k package=THT]
  R20 = Resistor [tolerance=±5% resistance=100k package=THT]
  R10 = Resistor [tolerance=±5% resistance=100k package=THT]
  R23 = Resistor [tolerance=±5% resistance=100k package=THT]
  JP11 = Header 4 [package=molex-1x4_lock]
  R24 = Resistor [tolerance=±5% resistance=10k package=THT]
  R11 = Resistor [tolerance=±5% resistance=10k package=THT]

nets:
  GND: Q4.E, JP3.1, Flyduino.GND, Q5.E, JP5.1, Q6.E, JP6.1, Q7.E, JP7.1, Q8.E, JP8.1, Q9.E, JP10.1, Q11.E, JP9.1, J1.GND, Q10.E, JP11.1
  N1: Q4.B, R23.Pin_0
  N2: Q4.C, JP3.4
  N3: JP3.2, JP5.2, JP6.2, JP7.2, JP8.2, JP10.2, JP9.2, J1.5V, JP11.2
  N4: JP3.3, R24.Pin_0
  N5: Flyduino.A3, R20.Pin_1
  N6: Flyduino.A2, R19.Pin_1
  N7: Flyduino.A1, R12.Pin_1
  N8: Flyduino.A0, R11.Pin_1
  N9: Flyduino.D13/SCK, R16.Pin_1
  N10: Flyduino.D12/MISO, R15.Pin_1
  N11: Flyduino.D11_PWM/MOSI, R24.Pin_1
  N12: Flyduino.D10_PWM/SS, R23.Pin_1
  N13: Flyduino.D9_PWM, R10.Pin_1
  N14: Flyduino.D8, R9.Pin_0
  N15: Flyduino.D7, R13.Pin_1
  N16: Flyduino.D6_PWM, R14.Pin_1
  N17: Flyduino.D5_PWM, R17.Pin_1
  N18: Flyduino.D4, R18.Pin_1
  N19: Flyduino.D3_PWM, R21.Pin_1
  N20: Flyduino.D2, R22.Pin_1
  N21: Q5.B, R10.Pin_0
  N22: Q5.C, JP11.4
  N23: JP5.3, R11.Pin_0
  N24: JP5.4, Q6.C
  N25: Q6.B, R12.Pin_0
  N26: JP6.3, R13.Pin_0
  N27: JP6.4, Q7.C
  N28: Q7.B, R14.Pin_0
  N29: JP7.3, R15.Pin_0
  N30: JP7.4, Q8.C
  N31: Q8.B, R16.Pin_0
  N32: JP8.3, R17.Pin_0
  N33: JP8.4, Q9.C
  N34: Q9.B, R18.Pin_0
  N35: JP10.3, R21.Pin_0
  N36: JP10.4, Q11.C
  N37: Q11.B, R22.Pin_0
  N38: JP9.3, R19.Pin_0
  N39: JP9.4, Q10.C
  N40: R9.Pin_1, JP11.3
  N41: Q10.B, R20.Pin_0

// code stored in the sketch: softpwm_sense_serial.ino
#include <SoftPWM.h>

int pin_pwm = 5;
int pin_pulse = 6;
int pwm_value = 64;
int target_rpm = 2000;

void setup()
{
  Serial.begin(9600);
  pinMode(pin_pulse, INPUT);
  digitalWrite(pin_pulse,HIGH);
  
  SoftPWMBegin();
  SoftPWMSet(pin_pwm, 0);
  SoftPWMSetFadeTime(pin_pwm, 100, 100);
  SoftPWMSet(pin_pwm, pwm_value);
}

void loop()
{
  unsigned long pulseDuration = pulseIn(pin_pulse, LOW);
  Serial.print("Duration: ");
  Serial.print(pulseDuration);
  Serial.print(" ");

  double frequency = 1000000/pulseDuration;
  Serial.print("Frequency:");
  Serial.print(frequency);
  Serial.print(" ");
  
  double rpm = frequency/2*60;
  Serial.print("RPM:");
  Serial.print(rpm);
  Serial.print(" ");
  
  if (rpm > target_rpm + 0.03 * target_rpm) {
    pwm_value = pwm_value + 10;
  }
  if (pwm_value > 254) {
    pwm_value = 254;
  }

  if (rpm < target_rpm - 0.03 * target_rpm) {
    pwm_value = pwm_value - 10;
  }
  
  if (pwm_value < 1) {
    pwm_value = 1;
  }

  Serial.print("PWM:");
  Serial.print(pwm_value);
  Serial.println();

  SoftPWMSet(pin_pwm, pwm_value);
}
