# Fritzing sketch UberPWM3 (saved by Fritzing 0.9.3b)
circuit board: 3.83436cm x 2.72244cm
breadboards: 1

parts:
  JP5 = Header 4 [package=molex-1x4_lock]
  JP2 = Header 4 [package=molex-1x4_lock]
  JP7 = Header 4 [package=molex-1x4_lock]
  JP1 = Header 4 [package=molex-1x4_lock]
  JP9 = Header 4 [package=molex-1x4_lock]
  JP3 = Header 4 [package=molex-1x4_lock]
  JP3_2 = Header 4 [package=molex-1x4_lock]
  JP0 = Header 4 [package=molex-1x4_lock]
  Bauteil1 = Arduino Pro Mini v13

nets:
  N1: JP5.1, JP2.1, JP7.1, JP1.1, JP9.1, JP3.1, JP3_2.1, JP0.1, Bauteil1.GND
  N2: JP5.2, JP2.2, JP7.2, JP1.2, JP9.2, JP3.2, JP3_2.2, JP0.2
  N3: JP5.3, Bauteil1.D13/SCK
  N4: JP5.4, Bauteil1.D12/MISO
  N5: JP2.3, Bauteil1.D7
  N6: JP2.4, Bauteil1.D6_PWM
  N7: JP7.3, Bauteil1.A0
  N8: JP7.4, Bauteil1.A1
  N9: JP1.3, Bauteil1.D4
  N10: JP1.4, Bauteil1.D5_PWM
  N11: JP9.3, Bauteil1.A2
  N12: JP9.4, Bauteil1.A3
  N13: JP3.3, Bauteil1.D8
  N14: JP3.4, Bauteil1.D9_PWM
  N15: JP3_2.3, Bauteil1.D11_PWM/MOSI
  N16: JP3_2.4, Bauteil1.D10_PWM/SS
  N17: JP0.3, Bauteil1.D2
  N18: JP0.4, Bauteil1.D3_PWM
