# Fritzing sketch UberPWM3_compact (saved by Fritzing 0.9.3b)
circuit board: 1.77902cm x 4.08364cm
breadboards: 1

parts:
  C2 = Electrolytic Capacitor [capacitance=1000μF package="0807 [SMD, electrolytic]"]
  Bauteil4 = Arduino Pro Mini v13
  C1 = Electrolytic Capacitor [capacitance=1000μF package="0807 [SMD, electrolytic]"]
  JP12 = Header 4 [package=molex-1x4_lock]
  JP11 = Header 4 [package=molex-1x4_lock]
  JP10 = Header 4 [package=molex-1x4_lock]
  JP15 = Header 4 [package=molex-1x4_lock]
  JP9 = Header 4 [package=molex-1x4_lock]
  JP8 = Header 4 [package=molex-1x4_lock]
  JP14 = Header 4 [package=molex-1x4_lock]
  JP13 = Header 4 [package=molex-1x4_lock]

nets:
  N1: C2.+, Bauteil4.GND, JP12.1, JP11.1, JP10.1, JP15.1, JP9.1, JP8.1, JP14.1, JP13.1
  N2: Bauteil4.A3, JP8.3
  N3: Bauteil4.A2, JP8.4
  N4: Bauteil4.A1, JP13.3
  N5: Bauteil4.A0, JP13.4
  N6: Bauteil4.D13/SCK, JP14.3
  N7: Bauteil4.D12/MISO, JP14.4
  N8: Bauteil4.D11_PWM/MOSI, JP15.3
  N9: Bauteil4.D10_PWM/SS, JP15.4
  N10: Bauteil4.D9_PWM, JP12.4
  N11: Bauteil4.D8, JP12.3
  N12: Bauteil4.D7, JP11.3
  N13: Bauteil4.D6_PWM, JP11.4
  N14: Bauteil4.D5_PWM, JP10.4
  N15: Bauteil4.D4, JP10.3
  N16: Bauteil4.D3_PWM, JP9.4
  N17: Bauteil4.D2, JP9.3
  N18: C1.+, JP12.2, JP11.2, JP10.2, JP15.2, JP9.2, JP8.2, JP14.2, JP13.2

custom parts:
  Arduino Pro Mini v13: It's blue! It's thin! It's the Arduino Pro Mini! SparkFun's minimal design approach to Arduino. This is a 5V Arduino running the 16MHz bootloader. Arduino Pro Mini does not come with connectors populated so that you can solder in any connector or wire with any orientation you need. We recommend first time Arduino users start with the Uno R3. It's a great board that will get you up and running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
  Header 4: Header 4 Standard 4-pin 0.1 header. Use with straight break away headers (SKU : PRT-00116), right angle break away headers (PRT-00553), swiss pins (PRT-00743), machine pins (PRT-00117), and female headers (PRT-00115). Molex polarized connector foot print use with SKU : PRT-08231 with associated crimp pins and housings. 1MM SMD Version SKU: PRT-10208
