# Fritzing sketch UberPWM4 (saved by Fritzing 0.9.3b)
circuit board: 7.40145cm x 5.14828cm
breadboards: 1

parts:
  FAN13 = Header 4 [package=molex-1x4_lock]
  FAN14 = Header 4 [package=molex-1x4_lock]
  FAN05 = Header 4 [package=molex-1x4_lock]
  FAN04 = Header 4 [package=molex-1x4_lock]
  FAN03 = Header 4 [package=molex-1x4_lock]
  FAN02 = Header 4 [package=molex-1x4_lock]
  FAN01 = Header 4 [package=molex-1x4_lock]
  FAN00 = Header 4 [package=molex-1x4_lock]
  FAN09 = Header 4 [package=molex-1x4_lock]
  FAN07 = Header 4 [package=molex-1x4_lock]
  FAN06 = Header 4 [package=molex-1x4_lock]
  FAN11 = Header 4 [package=molex-1x4_lock]
  FAN10 = Header 4 [package=molex-1x4_lock]
  FAN08 = Header 4 [package=molex-1x4_lock]
  FAN15 = Header 4 [package=molex-1x4_lock]
  FAN12 = Header 4 [package=molex-1x4_lock]
  Part3 = Arduino Mega 2560 (Rev3)
  RESET = Momentary Switch [package=ksa_sealed_tac_switch]

nets:
  N1: FAN13.1, FAN14.1, FAN05.1, FAN04.1, FAN03.1, FAN02.1, FAN01.1, FAN00.1, FAN09.1, FAN07.1, FAN06.1, FAN11.1, FAN10.1, FAN08.1, FAN15.1, FAN12.1
  N2: FAN13.2, FAN14.2, FAN05.2, FAN04.2, FAN03.2, FAN02.2, FAN01.2, FAN00.2, FAN09.2, FAN07.2, FAN06.2, FAN11.2, FAN10.2, FAN08.2, FAN15.2, FAN12.2
  N3: FAN13.3, Part3.A9
  N4: FAN13.4, Part3.D2_PWM
  N5: FAN14.3, Part3.A12
  N6: FAN14.4, Part3.D45
  N7: FAN05.3, Part3.D19/RX1
  N8: FAN05.4, Part3.D3_PWM
  N9: FAN04.3, Part3.D18/TX1
  N10: FAN04.4, Part3.D5_PWM
  N11: FAN03.3, Part3.D17_PWM/RX2
  N12: FAN03.4, Part3.D7_PWM
  N13: FAN02.3, Part3.D16_PWM/TX2
  N14: FAN02.4, Part3.D9_PWM
  N15: FAN01.3, Part3.D15/RX3
  N16: FAN01.4, Part3.D11_PWM
  N17: FAN00.3, Part3.D14/TX3
  N18: FAN00.4, Part3.D13_PWM
  N19: FAN09.3, Part3.A1
  N20: FAN09.4, Part3.D10_PWM
  N21: FAN07.3, Part3.D21/SCL
  N22: FAN07.4, Part3.D44
  N23: FAN06.3, Part3.D20/SDA
  N24: FAN06.4, Part3.D1_TX0
  N25: FAN11.3, Part3.A4
  N26: FAN11.4, Part3.D6_PWM
  N27: FAN10.3, Part3.A2
  N28: FAN10.4, Part3.D8_PWM
  N29: FAN08.3, Part3.A0
  N30: FAN08.4, Part3.D12_PWM
  N31: FAN15.3, Part3.A15
  N32: FAN15.4, Part3.D46
  N33: FAN12.3, Part3.A7
  N34: FAN12.4, Part3.D4_PWM
  N35: Part3.RESET, RESET.3, RESET.4
  N36: Part3.GND, RESET.1, RESET.2

notes:
  +-
  -+
