# Fritzing sketch UberPWM4_breadboard (saved by Fritzing 0.9.3b)
circuit board: 11.6693cm x 7.58244cm
breadboards: 1

parts:
  JP2 = Header 4 [package=molex-1x4_lock]
  JP0 = Header 4 [package=molex-1x4_lock]
  JP10 = Header 4 [package=molex-1x4_lock]
  JP11 = Header 4 [package=molex-1x4_lock]
  JP12 = Header 4 [package=molex-1x4_lock]
  JP13 = Header 4 [package=molex-1x4_lock]
  JP14 = Header 4 [package=molex-1x4_lock]
  JP15 = Header 4 [package=molex-1x4_lock]
  JP16 = Header 4 [package=molex-1x4_lock]
  JP8 = Header 4 [package=molex-1x4_lock]
  JP9 = Header 4 [package=molex-1x4_lock]
  JP5 = Header 4 [package=molex-1x4_lock]
  JP4 = Header 4 [package=molex-1x4_lock]
  JP7 = Header 4 [package=molex-1x4_lock]
  JP1 = Header 4 [package=molex-1x4_lock]
  JP3 = Header 4 [package=molex-1x4_lock]
  Part3 = Arduino Mega 2560 (Rev3)

nets:
  N1: JP2.1, JP0.1, JP10.1, JP11.1, JP12.1, JP13.1, JP14.1, JP15.1, JP16.1, JP8.1, JP9.1, JP5.1, JP4.1, JP7.1, JP1.1, JP3.1, Part3.GND
  N2: JP2.2, JP0.2, JP10.2, JP11.2, JP12.2, JP13.2, JP14.2, JP15.2, JP16.2, JP8.2, JP9.2, JP5.2, JP4.2, JP7.2, JP1.2, JP3.2, Part3.VIN
  N3: JP2.3, Part3.A9
  N4: JP2.4, Part3.D2_PWM
  N5: JP0.3, Part3.A12
  N6: JP0.4, Part3.D45
  N7: JP10.3, Part3.D19/RX1
  N8: JP10.4, Part3.D3_PWM
  N9: JP11.3, Part3.D18/TX1
  N10: JP11.4, Part3.D5_PWM
  N11: JP12.3, Part3.D17_PWM/RX2
  N12: JP12.4, Part3.D7_PWM
  N13: JP13.3, Part3.D16_PWM/TX2
  N14: JP13.4, Part3.D9_PWM
  N15: JP14.3, Part3.D15/RX3
  N16: JP14.4, Part3.D11_PWM
  N17: JP15.3, Part3.D14/TX3
  N18: JP15.4, Part3.D13_PWM
  N19: JP16.3, Part3.A1
  N20: JP16.4, Part3.D10_PWM
  N21: JP8.3, Part3.D21/SCL
  N22: JP8.4, Part3.D44
  N23: JP9.3, Part3.D20/SDA
  N24: JP9.4, Part3.D1_TX0
  N25: JP5.3, Part3.A4
  N26: JP5.4, Part3.D6_PWM
  N27: JP4.3, Part3.A2
  N28: JP4.4, Part3.D8_PWM
  N29: JP7.3, Part3.A0
  N30: JP7.4, Part3.D12_PWM
  N31: JP1.3, Part3.A15
  N32: JP1.4, Part3.D46
  N33: JP3.3, Part3.A7
  N34: JP3.4, Part3.D4_PWM
