# Fritzing sketch UberPWM5_PCB_v.5.0.8 (saved by Fritzing 0.9.6b)
circuit board: 9.95cm x 5.28cm
breadboards: 1

parts:
  FAN_13 = Header 4 [package=molex-1x4_lock]
  FAN_14 = Header 4 [package=molex-1x4_lock]
  FAN_5 = Header 4 [package=molex-1x4_lock]
  FAN_4 = Header 4 [package=molex-1x4_lock]
  FAN_3 = Header 4 [package=molex-1x4_lock]
  FAN_2 = Header 4 [package=molex-1x4_lock]
  FAN_1 = Header 4 [package=molex-1x4_lock]
  FAN_0 = Header 4 [package=molex-1x4_lock]
  FAN_9 = Header 4 [package=molex-1x4_lock]
  FAN_7 = Header 4 [package=molex-1x4_lock]
  FAN_6 = Header 4 [package=molex-1x4_lock]
  FAN_11 = Header 4 [package=molex-1x4_lock]
  FAN_10 = Header 4 [package=molex-1x4_lock]
  FAN_8 = Header 4 [package=molex-1x4_lock]
  FAN_15 = Header 4 [package=molex-1x4_lock]
  FAN_12 = Header 4 [package=molex-1x4_lock]
  Arduino_Mega_2560 = Arduino Mega 2560 (Rev3)
  12_V = Resistor [tolerance=±0.05% resistance=0 package=THT]
  GND = Resistor [tolerance=±0.05% resistance=0 package=THT]
  HLK-PM1 = HLK-PM12 [part_number=HLK-PM12]

nets:
  N1: FAN_13.1, FAN_14.1, FAN_5.1, FAN_4.1, FAN_3.1, FAN_2.1, FAN_1.1, FAN_0.1, FAN_9.1, FAN_7.1, FAN_6.1, FAN_11.1, FAN_10.1, FAN_8.1, FAN_15.1, FAN_12.1, Arduino_Mega_2560.GND, GND.Pin_1
  N2: FAN_13.2, FAN_14.2, FAN_5.2, FAN_4.2, FAN_3.2, FAN_2.2, FAN_1.2, FAN_0.2, FAN_9.2, FAN_7.2, FAN_6.2, FAN_11.2, FAN_10.2, FAN_8.2, FAN_15.2, FAN_12.2, 12_V.Pin_1
  N3: FAN_13.3, Arduino_Mega_2560.A10
  N4: FAN_13.4, Arduino_Mega_2560.D46
  N5: FAN_14.3, Arduino_Mega_2560.A12
  N6: FAN_14.4, Arduino_Mega_2560.D44
  N7: FAN_5.3, Arduino_Mega_2560.D19/RX1
  N8: FAN_5.4, Arduino_Mega_2560.D4_PWM
  N9: FAN_4.3, Arduino_Mega_2560.D18/TX1
  N10: FAN_4.4, Arduino_Mega_2560.D5_PWM
  N11: FAN_3.3, Arduino_Mega_2560.D17_PWM/RX2
  N12: FAN_3.4, Arduino_Mega_2560.D6_PWM
  N13: FAN_2.3, Arduino_Mega_2560.D16_PWM/TX2
  N14: FAN_2.4, Arduino_Mega_2560.D7_PWM
  N15: FAN_1.3, Arduino_Mega_2560.D15/RX3
  N16: FAN_1.4, Arduino_Mega_2560.D8_PWM
  N17: FAN_0.3, Arduino_Mega_2560.D14/TX3
  N18: FAN_0.4, Arduino_Mega_2560.D9_PWM
  N19: FAN_9.3, Arduino_Mega_2560.A2
  N20: FAN_9.4, Arduino_Mega_2560.D11_PWM
  N21: FAN_7.3, Arduino_Mega_2560.D21/SCL
  N22: FAN_7.4, Arduino_Mega_2560.D2_PWM
  N23: FAN_6.3, Arduino_Mega_2560.D20/SDA
  N24: FAN_6.4, Arduino_Mega_2560.D3_PWM
  N25: FAN_11.3, Arduino_Mega_2560.A6
  N26: FAN_11.4, Arduino_Mega_2560.D13_PWM
  N27: FAN_10.3, Arduino_Mega_2560.A4
  N28: FAN_10.4, Arduino_Mega_2560.D12_PWM
  N29: FAN_8.3, Arduino_Mega_2560.A0
  N30: FAN_8.4, Arduino_Mega_2560.D10_PWM
  N31: FAN_15.3, Arduino_Mega_2560.A14
  N32: FAN_15.4, Arduino_Mega_2560.D1_TX0
  N33: FAN_12.3, Arduino_Mega_2560.A8
  N34: FAN_12.4, Arduino_Mega_2560.D45
  N35: 12_V.Pin_0, HLK-PM1.+Vo
  N36: GND.Pin_0, HLK-PM1.-Vo

notes:
  ALFC
  v5.0.8

// code stored in the sketch: bridgehead3_Mega.ino
const int PINS_PULSE[] = {14, 15, 16, 17, 18, 19, SDA, SCL, A0, A1, A2, A4, A7, A9, A15, A12};
const int PINS_PWM[] = {1, 2, 3, 4, 5, 6, 7, 8, 9, 10, 11, 13, 44, 45, 46};
const int MICROSECONDS_IN_ONE_SECOND = 1000000;


void setup() {
    const int PWM_FREQUENCY_TARGET = 24000;

    // The base frequency for pins 2, 3, 5, 6, 7, 8, 9, 10, 11, 12, and 46 is 31250 Hz
    // So set a pin's PWM frequency of each clock to 31250 Hz / 1 = 31250 Hz
    setPwmFrequency( 2, 1);
    setPwmFrequency( 6, 1);
    setPwmFrequency( 9, 1);
    setPwmFrequency(11, 1);
    setPwmFrequency(44, 1);

    // The base frequency for pins 4 and 13 is 62500 Hz
    // Set pin 4's PWM frequency to 62500/8 = 7813 Hz
    setPwmFrequency(4, 2);

    // space out fan speeds a bit to avoid some resonance
    int pwms[16] = {38, 39, 40, 41, 42, 43, 44, 45, 46, 47, 48, 49, 50, 51, 52, 53};

    // Shuffle PWM values to load fans randomly
    for (int i = 0; i < 16 - 1; i++) {
        int j = random(0, 16 - i);

        int t = pwms[i];
        pwms[i] = pwms[j];
        pwms[j] = t;
    }

    // Send a start up pulse
    setPwms(pwms);

    // Initialize pulse pins
    for (int i = 0; i < 16; i++)     
        pinMode(PINS_PULSE[i], INPUT_PULLUP);

    const int SERIAL_BD_RATE = 19200;
    Serial.begin(SERIAL_BD_RATE);
    Serial.write("Setup done");
}

int* messageToPwms(String message) {
    // Caution: Non-reentrant return value.
    static int pwms[16];

    int separator_position;
    for (int i = 0; i < 16; i++) {
        // Determine next separator
        separator_position = message.indexOf(';');
  
        // Parse value left of a ';' 
        pwms[i] = message.substring(0, separator_position).toInt();

        // Strip part left of a ';' from message
        message = message.substring(separator_position + 1);
    }

    return pwms;
}

void logPulseIntervals() {
    String pulseDurations = "";

    // Collect pulse durations from all fans into a message
    for (int i = 0; i < 16; i++)
        pulseDurations = \
            pulseDurations + \
            String(
                float(MICROSECONDS_IN_ONE_SECOND) /
                pulseIn(PINS_PULSE[i], LOW, 200000)
            ) + \
            ";";

    // Log message to the host via the serial interface
    Serial.println(pulseDurations);
}

void setPwms(int pwms[]) {
    // Set PWM value to each fan
    for (byte channel_index = 0; channel_index < 16; channel_index++)
        analogWrite(PINS_PWM[channel_index], pwms[channel_index]);
}

String LAST_MESSAGE = "";
void loop() {
    // Get message from serial console
    String message = "";
    while (Serial.available())
        message.concat((char) Serial.read());

    if (message == "") {
        if (LAST_MESSAGE == "") {
            // We have never gotten a message.
            // So keep waiting for one.
            return;
        } else {
            // We have not gotten a message this time, but last time.
            // So use the last message as our current one.
            message = LAST_MESSAGE;
            // We already know that the current message equals last message.
            // So log the pulse intervals.
            logPulseIntervals();
        }
    } else {
        // We got a message this time.
        if (LAST_MESSAGE == message) {
            // This message was repeated by the host.
            // So log the pulse intervals.
            logPulseIntervals();            
        } else {
            // This message was new.
            // So update the last message.
            LAST_MESSAGE = message;
            // Also update the PWMs and the log pulse intervals.
            setPwms(messageToPwms(message));
            logPulseIntervals();
        }
    }

    Serial.println(".");
}

void setPwmFrequency(int pin, int divisor) {
    byte mode;

    if(pin == 4 || pin == 13) {
        switch(divisor) {
            case 1: mode = 0x01; break;
            case 8: mode = 0x02; break;
            case 64: mode = 0x03; break;
            case 256: mode = 0x04; break;
            case 1024: mode = 0x05; break;
            default: return;
        }
        TCCR0B = TCCR0B & B11111000 | mode;
        return;
    }

    if(pin == 11 || pin == 12) {
        switch(divisor) {
            case 1: mode = 0x01; break;
            case 8: mode = 0x02; break;
            case 64: mode = 0x03; break;
            case 256: mode = 0x04; break;
            case 1024: mode = 0x05; break;
            default: return;
        }
        TCCR1B = TCCR1B & B11111000 | mode;
        return;
    }

    if(pin == 9 || pin == 10) {
        switch(divisor) {
            case 1: mode = 0x01; break;
            case 8: mode = 0x02; break;
            case 32: mode = 0x03; break;
            case 64: mode = 0x04; break;
            case 128: mode = 0x05; break;
            case 256: mode = 0x06; break;
            case 1024: mode = 0x07; break;
            default: return;
        }
        TCCR2B = TCCR2B & B11111000 | mode;
        return;
    }

    if(pin == 2 || pin == 3 || pin == 5) {
        switch(divisor) {
            case 1: mode = 0x01; break;
            case 8: mode = 0x02; break;
            case 64: mode = 0x03; break;
            case 256: mode = 0x04; break;
            case 1024: mode = 0x05; break;
            default: return;
        }
        TCCR3B = TCCR3B & B11111000 | mode;
        return;
    }

    if(pin == 6 || pin == 7 || pin == 8) {
        switch(divisor) {
            case 1: mode = 0x01; break;
            case 8: mode = 0x02; break;
            case 64: mode = 0x03; break;
            case 256: mode = 0x04; break;
            case 1024: mode = 0x05; break;
            default: return;
        }
        TCCR4B = TCCR4B & B11111000 | mode;
        return;
    }

    if(pin == 44 || pin == 45 || pin == 46) {
        switch(divisor) {
            case 1: mode = 0x01; break;
            case 8: mode = 0x02; break;
            case 64: mode = 0x03; break;
            case 256: mode = 0x04; break;
            case 1024: mode = 0x05; break;
            default: return;
        }
        TCCR5B = TCCR5B & B11111000 | mode;
        return;
    }
}
